// Digital circuit Banco_de_registradores.dig as structural Verilog
module Banco_de_registradores (
  input  clk,
  input  [3:0] A,
  input  [3:0] B,
  input  [3:0] c,
  input  we,
  input  [31:0] Dado,
  output [31:0] s_a,
  output [31:0] s_b
);

  wire e0, e1, e2, e3, e4, e5, e6, e7, e8, e9, e10, e11, e12, e13, e14, e15;
  wire [31:0] s0, s1, s2, s3, s4, s5, s6, s7, s8, s9, s10, s11, s12, s13, s14, s15;

  Register #(.Bits(32)) register_1 (.D(Dado), .C(clk), .en(e0), .Q(s0));
  Register #(.Bits(32)) register_2 (.D(Dado), .C(clk), .en(e1), .Q(s1));
  Register #(.Bits(32)) register_3 (.D(Dado), .C(clk), .en(e2), .Q(s2));
  Register #(.Bits(32)) register_4 (.D(Dado), .C(clk), .en(e3), .Q(s3));
  Multiplexer #(.Selector_Bits(4), .Bits(32)) multiplexer_1 (
    .sel(A), .in_0(s0), .in_1(s1), .in_2(s2), .in_3(s3), .in_4(s4), .in_5(s5), .in_6(s6), .in_7(s7),
    .in_8(s8), .in_9(s9), .in_10(s10), .in_11(s11), .in_12(s12), .in_13(s13), .in_14(s14), .in_15(s15),
    .out(s_a));
  Register #(.Bits(32)) register_5 (.D(Dado), .C(clk), .en(e4), .Q(s4));
  Register #(.Bits(32)) register_6 (.D(Dado), .C(clk), .en(e5), .Q(s5));
  Register #(.Bits(32)) register_7 (.D(Dado), .C(clk), .en(e6), .Q(s6));
  Register #(.Bits(32)) register_8 (.D(Dado), .C(clk), .en(e7), .Q(s7));
  Multiplexer #(.Selector_Bits(4), .Bits(32)) multiplexer_2 (
    .sel(B), .in_0(s0), .in_1(s1), .in_2(s2), .in_3(s3), .in_4(s4), .in_5(s5), .in_6(s6), .in_7(s7),
    .in_8(s8), .in_9(s9), .in_10(s10), .in_11(s11), .in_12(s12), .in_13(s13), .in_14(s14), .in_15(s15),
    .out(s_b));
  Register #(.Bits(32)) register_9 (.D(Dado), .C(clk), .en(e8), .Q(s8));
  Register #(.Bits(32)) register_10 (.D(Dado), .C(clk), .en(e9), .Q(s9));
  Register #(.Bits(32)) register_11 (.D(Dado), .C(clk), .en(e10), .Q(s10));
  Register #(.Bits(32)) register_12 (.D(Dado), .C(clk), .en(e11), .Q(s11));
  Demultiplexer #(.Selector_Bits(4)) demultiplexer_1 (
    .sel(c), .in(we), .out_0(e0), .out_1(e1), .out_2(e2), .out_3(e3), .out_4(e4), .out_5(e5), .out_6(e6),
    .out_7(e7), .out_8(e8), .out_9(e9), .out_10(e10), .out_11(e11), .out_12(e12), .out_13(e13), .out_14(e14),
    .out_15(e15));
  Register #(.Bits(32)) register_13 (.D(Dado), .C(clk), .en(e12), .Q(s12));
  Register #(.Bits(32)) register_14 (.D(Dado), .C(clk), .en(e13), .Q(s13));
  Register #(.Bits(32)) register_15 (.D(Dado), .C(clk), .en(e14), .Q(s14));
  Register #(.Bits(32)) register_16 (.D(Dado), .C(clk), .en(e15), .Q(s15));

  // Other names for the same wires on the sheet: C_t[31:0] = Dado
endmodule
