// Digital circuit MICO XII.dig as structural Verilog
module MICO_XII (
  input  clk
);

  wire banco_de_registradores_1_p8;
  wire [15:0] add_1_s, banco_de_registradores_1_p6, IP_q, multiplexer_1_out;
  wire [15:1] undriven;
  wire [31:0] banco_de_registradores_1_p7, bitextender_1_out, MI_d, multiplexer_2_out;

  Add #(.Bits(16)) add_1 (.a(IP_q), .b({undriven, 1'b1}), .c_i(1'b0), .s(add_1_s));  // open: c_o
  Multiplexer #(.Selector_Bits(2), .Bits(16)) multiplexer_1 (
    .in_0(add_1_s), .in_2(banco_de_registradores_1_p6), .out(multiplexer_1_out));  // open: sel, in_1, in_3
  Register #(.Bits(16)) IP (.D(multiplexer_1_out), .C(clk), .en(1'b1), .Q(IP_q));
  ROM #(.Bits(32)) MI (.A(IP_q[1:0]), .D(MI_d));  // open: sel
  // Banco_de_registradores banco_de_registradores_1: pin names not known; wires that end beside it: clk, MI_d[7:4], MI_d[11:8], MI_d[15:12], MI_d[3:0], banco_de_registradores_1_p6, banco_de_registradores_1_p7, banco_de_registradores_1_p8
  BitExtender #(.inputBits(16), .outputBits(32)) bitextender_1 (.in(MI_d[31:16]), .out(bitextender_1_out));
  Multiplexer #(.Bits(32)) multiplexer_2 (
    .sel(banco_de_registradores_1_p8), .in_0(banco_de_registradores_1_p7), .in_1(bitextender_1_out),
    .out(multiplexer_2_out));
  // ULA ula_1: pin names not known; wires that end beside it: banco_de_registradores_1_p6, multiplexer_2_out
  RAMDualPort #(.AddrBits(24), .Bits(32)) ramdualport_1 ();  // open: A, Din, str, C, ld, D
  Seven_Seg seven_seg_1 ();  // open: a, b, c, d, e, f, g, dp
  // Pins of 2 and 16 bits meet at IP_q
  // Pins of 1 and 16 bits meet at {undriven, 1'b1}
endmodule
