// Digital circuit ULA.dig as structural Verilog
module ULA (
  input  [31:0] A,
  input  [31:0] B,
  input  [3:0] FUN,
  output [31:0] R
);

  wire [31:0] add_1_s, and_1_out, Direita_out, Esquerda_out, not_1_out, or_1_out, sub_1_s, xor_1_out;

  Add #(.Bits(32)) add_1 (.a(A), .b(B), .c_i(1'b0), .s(add_1_s));  // open: c_o
  Sub #(.Bits(32)) sub_1 (.a(A), .b(B), .c_i(1'b0), .s(sub_1_s));  // open: c_o
  BarrelShifter #(.Bits(32)) Esquerda (.in(A), .shift(1'b1), .out(Esquerda_out));
  BarrelShifter #(.Bits(32)) Direita (.in(A), .shift(1'b1), .out(Direita_out));
  assign and_1_out = A & B;  // And and_1, 32 bits wide
  assign or_1_out = A | B;  // Or or_1, 32 bits wide
  assign xor_1_out = A ^ B;  // XOr xor_1, 32 bits wide
  assign not_1_out = ~A;  // Not not_1, 32 bits wide
  Multiplexer #(.Bits(32), .Selector_Bits(3)) multiplexer_1 (
    .sel(FUN[2:0]), .in_0(add_1_s), .in_1(sub_1_s), .in_2(Esquerda_out), .in_3(Direita_out),
    .in_4(and_1_out), .in_5(or_1_out), .in_6(xor_1_out), .in_7(not_1_out), .out(R));
  // Pins of 3 and 4 bits meet at FUN
  // Pins of 1 and 32 bits meet at {32{1'b0}}
  // Pins of 1 and 32 bits meet at {32{1'b0}}
endmodule
